# Fritzing sketch bathroom_fan (saved by Fritzing 0.9.3b)
circuit board: 8.46667cm x 5.64444cm
perfboards: 1

parts:
  WeMos_D1_Mini1 = WeMos D1 Mini
  Q1 = Basic FET P-Channel [part_number=IRLZ44N package="TO220 [THT]"]
  J1 = Camdenboss CTB0158-2 [part_number=CTB0158-2 package=THT]
  J2 = Camdenboss CTB0158-2 [part_number=CTB0158-2 package=THT]
  J3 = dht22 [package=THT]
  J4 = dht22 [package=THT]
  R2 = Resistor [tolerance=±1% resistance=270 package=THT]
  U1 = Voltage Regulator [package=to220-adj]
  R1 = Resistor [tolerance=±1% resistance=1k package=THT]
  R3 = Resistor [tolerance=±1% resistance=100k package=THT]

nets (from the breadboard view):
  VCC: WeMos_D1_Mini1.5V, J3.vcc, J4.vcc, U1.IN, R3.Pin_0
  N1: WeMos_D1_Mini1.D5, J3.data, J4.data
  N2: WeMos_D1_Mini1.D7, Q1.gate, R1.Pin_1
  GND: WeMos_D1_Mini1.G, J1.pin1, J2.pin2, J3.gnd, J4.gnd, R2.Pin_0, R1.Pin_0
  N3: Q1.drain, J2.pin1
  N4: Q1.source, J1.pin2, U1.OUT
  N5: R2.Pin_1, U1.ADJ, R3.Pin_1
